// Logisim project myCPU.circ as structural Verilog: 22 circuits, main circuit main
module main (
  input  in_1,
  input  in_2,
  output [17:0] out_3,
  output [3:0] out_4,
  output [3:0] out_5,
  output [17:0] out_6,
  output [17:0] out_7,
  output [17:0] out_8,
  output [17:0] out_9,
  output [17:0] out_10,
  output [17:0] out_11,
  output [1:0] out_12,
  output out_13,
  output [17:0] out_14
);

  wire alu_1_carry_out, and_2_out, and_3_out, and_4_out, and_5_out, and_6_out, and_7_out, clock,
       CompareOperation, controlled_buffer_1_out, controlled_buffer_3_out, controlled_buffer_4_out,
       controlled_buffer_5_out, controlled_buffer_6_out, controlled_buffer_7_out, counter_2_q,
       decoder_2_out0, decoder_2_out2, decoder_3_out0, decoder_3_out2, decoder_4_out0, decoder_4_out1,
       decoder_5_out0, decoder_5_out3, decoder_6_out1, decoder_6_out3, is_ALU, is_CMP, is_JUMP, isImmediate,
       JA, JB, JBE, JE, JEA, JUMP, JUMP_i, memory_read, memory_write, multiplexer_1_out, multiplexer_3_out,
       multiplexer_4_out, multiplexer_5_out, multiplexer_6_out, multiplexer_7_out, multiplexer_8_out, next,
       next_ALU, next_CMP, next_LD, next_ST, not_1_out, not_2_out, or_1_out, pc_enable, register_write,
       register_write_ALU, register_write_LD, write_register_enable;
  wire [1:0] alu_operation, compare_1_cf, counter_1_q, counter_3_q, counter_4_q, counter_5_q;
  wire [1:1] and_1_out;
  wire [2:0] jump_type;
  wire [3:0] dest_st_src1, op1, src1;
  wire [5:0] imm6;
  wire [9:0] address10;
  wire [17:0] address18, data_output, extend10to18_1_out_2, imm18, multiplexer_2_out, rom_1_data;

  Clock clock_1 (.out(clock));
  or or_1 (or_1_out, JUMP_i, next);
  Multiplexer #(.enable("false")) multiplexer_1 (.in0(1'b0), .in1(clock), .out(multiplexer_1_out), .sel(or_1_out));
  assign controlled_buffer_1_out = pc_enable ? multiplexer_1_out : 1'bz;  // Controlled_Buffer controlled_buffer_1
  Multiplexer #(.width(18), .enable("false")) multiplexer_2 (
    .in0(out_10), .in1(data_output), .out(multiplexer_2_out), .sel(memory_read));
  Decoder #(.select(3)) decoder_1 (
    .out0(JUMP), .out1(JE), .out2(JA), .out3(JB), .out4(JEA), .out5(JBE), .sel(jump_type), .en(is_JUMP));  // open: out6, out7
  or or_2 (CompareOperation, JEA, JA, JE, JB, JBE);
  ProgramCounter programcounter_1 (
    .in_1(next), .in_2(JUMP_i), .in_3(controlled_buffer_1_out), .\input (out_14), .reset(in_2),
    .\output (out_3));
  RAM #(.addrWidth(10), .dataWidth(18), .bus("separate")) ram_1 (
    .addr(address10), .din(out_11), .data(data_output), .str(memory_write), .sel(1'b1), .clk(clock),
    .ld(memory_read), .clr(1'b0));
  Multiplexer #(.enable("false")) multiplexer_3 (
    .in0(1'b0), .in1(write_register_enable), .out(multiplexer_3_out), .sel(register_write));
  Compare compare_1 (.in_1(out_6), .in_2(out_11), .ZF(compare_1_cf[1]), .CF(compare_1_cf[0]));
  Register #(.width(2)) register_1 (.D(compare_1_cf), .Q(out_12), .clk(clock));  // open: en, clr
  ROM #(.addrWidth(18), .dataWidth(18)) rom_1 (.addr(out_3), .data(rom_1_data), .sel(1'b1));
  registerFile registerfile_1 (
    .read_register_1(out_4), .read_register_2(out_5), .Write_register(dest_st_src1),
    .write_data(multiplexer_2_out), .read_data_1(out_6), .read_data_2(out_11), .regWrite(multiplexer_3_out),
    .clock(clock), .clear(in_1));
  controlUnit controlunit_1 (
    .register1_input(out_6), .register2_input(out_11), .isImmediate(isImmediate), .alu_op(alu_operation),
    .address18(address18), .imm18(imm18), .isALU(is_ALU), .write_register(write_register_enable),
    .is_cmp_successful(out_13), .is_cmp(is_CMP), .write_memory(memory_write), .read_memory(memory_read),
    .is_jump(is_JUMP), .src2_op2(out_5), .src1(src1), .input_18(rom_1_data), .op1(op1),
    .dest_st_src1(dest_st_src1), .imm6(imm6), .address10(address10), .jump_type(jump_type));
  not not_1 (not_1_out, out_12[0]);
  not not_2 (not_2_out, out_12[1]);
  and and_1 (and_1_out[1], out_13, CompareOperation);
  Multiplexer #(.enable("false")) multiplexer_4 (.in0(1'b0), .in1(not_1_out), .out(multiplexer_4_out), .sel(is_JUMP));
  Multiplexer #(.enable("false")) multiplexer_5 (.in0(1'b0), .in1(not_2_out), .out(multiplexer_5_out), .sel(is_JUMP));
  Multiplexer #(.enable("false")) multiplexer_6 (.in0(1'b0), .in1(out_12[0]), .out(multiplexer_6_out), .sel(is_JUMP));
  Multiplexer #(.enable("false")) multiplexer_7 (.in0(1'b0), .in1(out_12[0]), .out(multiplexer_7_out), .sel(is_JUMP));
  Multiplexer #(.enable("false")) multiplexer_8 (.in0(1'b0), .in1(out_12[1]), .out(multiplexer_8_out), .sel(is_JUMP));
  extend10to18 extend10to18_1 (.in_1(address10), .out_2(extend10to18_1_out_2));
  Multiplexer #(.select(2), .width(18), .enable("false")) multiplexer_9 (
    .in0(18'h1), .in1(extend10to18_1_out_2), .in2(extend10to18_1_out_2), .in3(18'h1), .out(out_14),
    .sel({and_1_out[1], JUMP}));
  and and_2 (and_2_out, JEA, multiplexer_4_out);
  and and_3 (and_3_out, JA, multiplexer_4_out, multiplexer_5_out);
  and and_4 (and_4_out, JE, multiplexer_4_out, multiplexer_5_out);
  and and_5 (and_5_out, JB, multiplexer_5_out, multiplexer_6_out);
  and and_6 (and_6_out, JBE, multiplexer_7_out, multiplexer_8_out);
  or or_3 (out_13, and_2_out, and_3_out, and_4_out, and_5_out, and_6_out);
  Multiplexer #(.select(2), .width(4), .enable("false")) multiplexer_10 (
    .in0(src1), .in1(op1), .in2(dest_st_src1), .out(out_4), .sel({memory_write, is_CMP}));  // open: in3
  ALU alu_1 (.A(out_6), .B(out_9), .\output (out_8), .carry_out(alu_1_carry_out), .ALU_operation(alu_operation));
  or or_4 (register_write, register_write_ALU, register_write_LD);
  or or_5 (pc_enable, next_ALU, next_LD, next_ST, next_CMP, JUMP_i);
  or or_6 (next, next_ALU, next_LD, next_ST, next_CMP);
  assign out_10 = is_ALU ? out_8 : 18'bz;  // Controlled_Buffer controlled_buffer_2
  and and_7 (and_7_out, isImmediate, is_ALU);
  Multiplexer #(.width(18), .enable("false")) multiplexer_11 (.in0(out_11), .in1(imm18), .out(out_9), .sel(and_7_out));
  assign controlled_buffer_3_out = is_ALU ? clock : 1'bz;  // Controlled_Buffer controlled_buffer_3
  assign controlled_buffer_4_out = memory_read ? clock : 1'bz;  // Controlled_Buffer controlled_buffer_4
  Counter #(.width(2), .max('h3)) counter_1 (
    .Q(counter_1_q), .clk(controlled_buffer_4_out));  // open: load, D, count, carry, clr
  assign controlled_buffer_5_out = memory_write ? clock : 1'bz;  // Controlled_Buffer controlled_buffer_5
  Counter #(.width(1), .max('h1)) counter_2 (
    .Q(counter_2_q), .clk(controlled_buffer_5_out));  // open: load, D, count, carry, clr
  assign controlled_buffer_6_out = is_CMP ? clock : 1'bz;  // Controlled_Buffer controlled_buffer_6
  assign controlled_buffer_7_out = is_JUMP ? clock : 1'bz;  // Controlled_Buffer controlled_buffer_7
  Counter #(.width(2), .max('h2)) counter_3 (
    .Q(counter_3_q), .clk(controlled_buffer_3_out));  // open: load, D, count, carry, clr
  Decoder #(.select(2), .enable("false")) decoder_2 (
    .out0(decoder_2_out0), .out1(register_write_ALU), .out2(decoder_2_out2), .sel(counter_3_q));  // open: out3
  Decoder #(.select(2), .enable("false")) decoder_3 (
    .out0(decoder_3_out0), .out1(register_write_LD), .out2(decoder_3_out2), .sel(counter_1_q));  // open: out3
  Decoder #(.enable("false")) decoder_4 (.out0(decoder_4_out0), .out1(decoder_4_out1), .sel(counter_2_q));
  Counter #(.width(2), .max('h3)) counter_4 (
    .Q(counter_4_q), .clk(controlled_buffer_6_out));  // open: load, D, count, carry, clr
  Decoder #(.select(2)) decoder_5 (
    .out0(decoder_5_out0), .out3(decoder_5_out3), .sel(counter_4_q));  // open: out1, out2, en
  Decoder #(.select(2)) decoder_6 (
    .out1(decoder_6_out1), .out3(decoder_6_out3), .sel(counter_5_q));  // open: out0, out2, en
  Counter #(.width(2), .max('h3)) counter_5 (
    .Q(counter_5_q), .clk(controlled_buffer_7_out));  // open: load, D, count, carry, clr
  assign next_ALU = decoder_2_out0 ? 1'b0 : 1'bz;  // Controlled_Buffer controlled_buffer_8
  assign next_ALU = decoder_2_out2 ? 1'b1 : 1'bz;  // Controlled_Buffer controlled_buffer_9
  assign next_LD = decoder_3_out0 ? 1'b0 : 1'bz;  // Controlled_Buffer controlled_buffer_10
  assign next_LD = decoder_3_out2 ? 1'b1 : 1'bz;  // Controlled_Buffer controlled_buffer_11
  assign next_ST = decoder_4_out0 ? 1'b0 : 1'bz;  // Controlled_Buffer controlled_buffer_12
  assign next_ST = decoder_4_out1 ? 1'b1 : 1'bz;  // Controlled_Buffer controlled_buffer_13
  assign next_CMP = decoder_5_out0 ? 1'b0 : 1'bz;  // Controlled_Buffer controlled_buffer_14
  assign next_CMP = decoder_5_out3 ? 1'b1 : 1'bz;  // Controlled_Buffer controlled_buffer_15
  assign JUMP_i = decoder_6_out1 ? 1'b1 : 1'bz;  // Controlled_Buffer controlled_buffer_16
  assign JUMP_i = decoder_6_out3 ? 1'b0 : 1'bz;  // Controlled_Buffer controlled_buffer_17

  assign out_7 = out_6;
  // also tied to GND on the sheet: alu_1_carry_out

  // Other names for the same wires on the sheet: CF_ZF[1:0] = out_12; clear = in_1; cmpsc = out_13;
  //   input[17:0] = out_14; pc_enable_ALU = next_ALU; pc_enable_CMP = next_CMP; pc_enable_JUMP = JUMP_i;
  //   pc_enable_LD = next_LD; pc_enable_ST = next_ST; read_reg1[3:0] = out_4; register1_value[17:0] = out_6;
  //   register2_value[17:0] = out_11; register_write_data[17:0] = out_10; result_ALU[17:0] = out_8;
  //   second_input_alu[17:0] = out_9; read_reg2[3:0] = out_5; src2_op2[3:0] = out_5

  // Notes on the sheet:
  //   COMPARE JUMP
  //   contents of rom_1 (hex, n*v repeats v):
  //   1402 4c4e 9e09 c088 10c4c 15d50 1940c 1dff4 20067 24032 28014 2c388 30220 343da 3800c
  //   ALU FSM
  //   LD FSM
  //   ST FSM
  //   COMPARE FSM
  //   JUMP FSM
endmodule

// REGISTER
module registerFile (
  input  [3:0] read_register_1,
  input  [3:0] read_register_2,
  input  [3:0] Write_register,
  input  [17:0] write_data,
  input  regWrite,
  input  clock,
  input  clear,
  output [17:0] read_data_1,
  output [17:0] read_data_2
);

  wire and_1_out, and_2_out, and_3_out, and_4_out, and_5_out, and_6_out, and_7_out, and_8_out, and_9_out,
       and_10_out, and_11_out, and_12_out, and_13_out, and_14_out, and_15_out, and_16_out, decoder_1_out0,
       decoder_1_out1, decoder_1_out2, decoder_1_out3, decoder_1_out4, decoder_1_out5, decoder_1_out6,
       decoder_1_out7, decoder_1_out8, decoder_1_out9, decoder_1_out10, decoder_1_out11, decoder_1_out12,
       decoder_1_out13, decoder_1_out14, decoder_1_out15;
  wire [17:0] n18bitsregister_1_out_5, n18bitsregister_2_out_5, n18bitsregister_3_out_5,
       n18bitsregister_4_out_5, n18bitsregister_5_out_5, n18bitsregister_6_out_5, n18bitsregister_7_out_5,
       n18bitsregister_8_out_5, n18bitsregister_9_out_5, n18bitsregister_10_out_5, n18bitsregister_11_out_5,
       n18bitsregister_12_out_5, n18bitsregister_13_out_5, n18bitsregister_14_out_5,
       n18bitsregister_15_out_5, n18bitsregister_16_out_5;

  Decoder #(.select(4), .enable("false")) decoder_1 (
    .out0(decoder_1_out0), .out1(decoder_1_out1), .out2(decoder_1_out2), .out3(decoder_1_out3),
    .out4(decoder_1_out4), .out5(decoder_1_out5), .out6(decoder_1_out6), .out7(decoder_1_out7),
    .out8(decoder_1_out8), .out9(decoder_1_out9), .out10(decoder_1_out10), .out11(decoder_1_out11),
    .out12(decoder_1_out12), .out13(decoder_1_out13), .out14(decoder_1_out14), .out15(decoder_1_out15),
    .sel(Write_register));
  and and_1 (and_1_out, regWrite, decoder_1_out0);
  and and_2 (and_2_out, regWrite, decoder_1_out1);
  and and_3 (and_3_out, regWrite, decoder_1_out2);
  and and_4 (and_4_out, regWrite, decoder_1_out3);
  and and_5 (and_5_out, regWrite, decoder_1_out4);
  and and_6 (and_6_out, regWrite, decoder_1_out5);
  and and_7 (and_7_out, regWrite, decoder_1_out6);
  and and_8 (and_8_out, regWrite, decoder_1_out7);
  _18BitsRegister u_18bitsregister_1 (
    .in_1(write_data), .enable(and_1_out), .clear(clear), .clock(clock), .out_5(n18bitsregister_1_out_5));
  _18BitsRegister u_18bitsregister_2 (
    .in_1(write_data), .enable(and_2_out), .clear(clear), .clock(clock), .out_5(n18bitsregister_2_out_5));
  _18BitsRegister u_18bitsregister_3 (
    .in_1(write_data), .enable(and_3_out), .clear(clear), .clock(clock), .out_5(n18bitsregister_3_out_5));
  _18BitsRegister u_18bitsregister_4 (
    .in_1(write_data), .enable(and_4_out), .clear(clear), .clock(clock), .out_5(n18bitsregister_4_out_5));
  _18BitsRegister u_18bitsregister_5 (
    .in_1(write_data), .enable(and_5_out), .clear(clear), .clock(clock), .out_5(n18bitsregister_5_out_5));
  _18BitsRegister u_18bitsregister_6 (
    .in_1(write_data), .enable(and_6_out), .clear(clear), .clock(clock), .out_5(n18bitsregister_6_out_5));
  _18BitsRegister u_18bitsregister_7 (
    .in_1(write_data), .enable(and_7_out), .clear(clear), .clock(clock), .out_5(n18bitsregister_7_out_5));
  _18BitsRegister u_18bitsregister_8 (
    .in_1(write_data), .enable(and_8_out), .clear(clear), .clock(clock), .out_5(n18bitsregister_8_out_5));
  and and_9 (and_9_out, regWrite, decoder_1_out8);
  and and_10 (and_10_out, regWrite, decoder_1_out9);
  and and_11 (and_11_out, regWrite, decoder_1_out10);
  and and_12 (and_12_out, regWrite, decoder_1_out11);
  and and_13 (and_13_out, regWrite, decoder_1_out12);
  and and_14 (and_14_out, regWrite, decoder_1_out13);
  and and_15 (and_15_out, regWrite, decoder_1_out14);
  and and_16 (and_16_out, regWrite, decoder_1_out15);
  _18BitsRegister u_18bitsregister_9 (
    .in_1(write_data), .enable(and_9_out), .clear(clear), .clock(clock), .out_5(n18bitsregister_9_out_5));
  _18BitsRegister u_18bitsregister_10 (
    .in_1(write_data), .enable(and_10_out), .clear(clear), .clock(clock), .out_5(n18bitsregister_10_out_5));
  _18BitsRegister u_18bitsregister_11 (
    .in_1(write_data), .enable(and_11_out), .clear(clear), .clock(clock), .out_5(n18bitsregister_11_out_5));
  _18BitsRegister u_18bitsregister_12 (
    .in_1(write_data), .enable(and_12_out), .clear(clear), .clock(clock), .out_5(n18bitsregister_12_out_5));
  _18BitsRegister u_18bitsregister_13 (
    .in_1(write_data), .enable(and_13_out), .clear(clear), .clock(clock), .out_5(n18bitsregister_13_out_5));
  _18BitsRegister u_18bitsregister_14 (
    .in_1(write_data), .enable(and_14_out), .clear(clear), .clock(clock), .out_5(n18bitsregister_14_out_5));
  _18BitsRegister u_18bitsregister_15 (
    .in_1(write_data), .enable(and_15_out), .clear(clear), .clock(clock), .out_5(n18bitsregister_15_out_5));
  _18BitsRegister u_18bitsregister_16 (
    .in_1(write_data), .enable(and_16_out), .clear(clear), .clock(clock), .out_5(n18bitsregister_16_out_5));
  Multiplexer #(.select(4), .width(18), .enable("false")) multiplexer_1 (
    .in0(n18bitsregister_1_out_5), .in1(n18bitsregister_2_out_5), .in2(n18bitsregister_3_out_5),
    .in3(n18bitsregister_4_out_5), .in4(n18bitsregister_5_out_5), .in5(n18bitsregister_6_out_5),
    .in6(n18bitsregister_7_out_5), .in7(n18bitsregister_8_out_5), .in8(n18bitsregister_9_out_5),
    .in9(n18bitsregister_10_out_5), .in10(n18bitsregister_11_out_5), .in11(n18bitsregister_12_out_5),
    .in12(n18bitsregister_13_out_5), .in13(n18bitsregister_14_out_5), .in14(n18bitsregister_15_out_5),
    .in15(n18bitsregister_16_out_5), .out(read_data_1), .sel(read_register_1));
  Multiplexer #(.select(4), .width(18), .enable("false")) multiplexer_2 (
    .in0(n18bitsregister_1_out_5), .in1(n18bitsregister_2_out_5), .in2(n18bitsregister_3_out_5),
    .in3(n18bitsregister_4_out_5), .in4(n18bitsregister_5_out_5), .in5(n18bitsregister_6_out_5),
    .in6(n18bitsregister_7_out_5), .in7(n18bitsregister_8_out_5), .in8(n18bitsregister_9_out_5),
    .in9(n18bitsregister_10_out_5), .in10(n18bitsregister_11_out_5), .in11(n18bitsregister_12_out_5),
    .in12(n18bitsregister_13_out_5), .in13(n18bitsregister_14_out_5), .in14(n18bitsregister_15_out_5),
    .in15(n18bitsregister_16_out_5), .out(read_data_2), .sel(read_register_2));
endmodule

module fullComparator (
  input  a,
  input  b,
  input  gt,
  input  lt,
  input  eq,
  output gt_out,
  output lt_out,
  output eq_out
);

  wire and_1_out, and_2_out, and_3_out, and_4_out, and_5_out, and_6_out, not_1_out, not_2_out, not_3_out,
       not_4_out, or_1_out;

  not not_1 (not_1_out, b);
  not not_2 (not_2_out, a);
  and and_1 (and_1_out, a, b);
  not not_3 (not_3_out, a);
  and and_2 (and_2_out, not_3_out, not_4_out);
  not not_4 (not_4_out, b);
  and and_3 (and_3_out, a, not_1_out);
  and and_4 (and_4_out, and_3_out, eq);
  and and_5 (and_5_out, eq, and_6_out);
  and and_6 (and_6_out, not_2_out, b);
  or or_1 (or_1_out, and_1_out, and_2_out);
  or or_2 (gt_out, and_4_out, gt);
  or or_3 (lt_out, and_5_out, lt);
  and and_7 (eq_out, eq, or_1_out);
endmodule

module halfComparator (
  input  A,
  input  B,
  output gt_out,
  output lt_out,
  output eq_out
);

  wire and_1_out, and_2_out, not_1_out, not_2_out, not_3_out, not_4_out;

  not not_1 (not_1_out, B);
  not not_2 (not_2_out, A);
  and and_1 (and_1_out, A, B);
  not not_3 (not_3_out, A);
  and and_2 (and_2_out, not_3_out, not_4_out);
  not not_4 (not_4_out, B);
  and and_3 (gt_out, A, not_1_out);
  and and_4 (lt_out, not_2_out, B);
  or or_1 (eq_out, and_1_out, and_2_out);
endmodule

module _18bitComparator (
  input  [17:0] b,
  input  [17:0] a,
  output gt,
  output lt,
  output eq
);

  wire fullcomparator_1_eq_out, fullcomparator_1_gt_out, fullcomparator_1_lt_out, fullcomparator_2_eq_out,
       fullcomparator_2_gt_out, fullcomparator_2_lt_out, fullcomparator_3_eq_out, fullcomparator_3_gt_out,
       fullcomparator_3_lt_out, fullcomparator_4_eq_out, fullcomparator_4_gt_out, fullcomparator_4_lt_out,
       fullcomparator_5_eq_out, fullcomparator_5_gt_out, fullcomparator_5_lt_out, fullcomparator_6_eq_out,
       fullcomparator_6_gt_out, fullcomparator_6_lt_out, fullcomparator_7_eq_out, fullcomparator_7_gt_out,
       fullcomparator_7_lt_out, fullcomparator_8_eq_out, fullcomparator_8_gt_out, fullcomparator_8_lt_out,
       fullcomparator_9_eq_out, fullcomparator_9_gt_out, fullcomparator_9_lt_out, fullcomparator_10_eq_out,
       fullcomparator_10_gt_out, fullcomparator_10_lt_out, fullcomparator_11_eq_out,
       fullcomparator_11_gt_out, fullcomparator_11_lt_out, fullcomparator_12_eq_out,
       fullcomparator_12_gt_out, fullcomparator_12_lt_out, fullcomparator_13_eq_out,
       fullcomparator_13_gt_out, fullcomparator_13_lt_out, fullcomparator_14_eq_out,
       fullcomparator_14_gt_out, fullcomparator_14_lt_out, fullcomparator_15_eq_out,
       fullcomparator_15_gt_out, fullcomparator_15_lt_out, fullcomparator_16_eq_out,
       fullcomparator_16_gt_out, fullcomparator_16_lt_out, halfcomparator_1_eq_out, halfcomparator_1_gt_out,
       halfcomparator_1_lt_out;

  halfComparator halfcomparator_1 (
    .A(a[17]), .B(b[17]), .gt_out(halfcomparator_1_gt_out), .lt_out(halfcomparator_1_lt_out),
    .eq_out(halfcomparator_1_eq_out));
  fullComparator fullcomparator_1 (
    .a(a[13]), .b(b[13]), .gt(fullcomparator_12_gt_out), .lt(fullcomparator_12_lt_out),
    .eq(fullcomparator_12_eq_out), .gt_out(fullcomparator_1_gt_out), .lt_out(fullcomparator_1_lt_out),
    .eq_out(fullcomparator_1_eq_out));
  fullComparator fullcomparator_2 (
    .a(a[9]), .b(b[9]), .gt(fullcomparator_13_gt_out), .lt(fullcomparator_13_lt_out),
    .eq(fullcomparator_13_eq_out), .gt_out(fullcomparator_2_gt_out), .lt_out(fullcomparator_2_lt_out),
    .eq_out(fullcomparator_2_eq_out));
  fullComparator fullcomparator_3 (
    .a(a[5]), .b(b[5]), .gt(fullcomparator_14_gt_out), .lt(fullcomparator_14_lt_out),
    .eq(fullcomparator_14_eq_out), .gt_out(fullcomparator_3_gt_out), .lt_out(fullcomparator_3_lt_out),
    .eq_out(fullcomparator_3_eq_out));
  fullComparator fullcomparator_4 (
    .a(a[16]), .b(b[16]), .gt(halfcomparator_1_gt_out), .lt(halfcomparator_1_lt_out),
    .eq(halfcomparator_1_eq_out), .gt_out(fullcomparator_4_gt_out), .lt_out(fullcomparator_4_lt_out),
    .eq_out(fullcomparator_4_eq_out));
  fullComparator fullcomparator_5 (
    .a(a[12]), .b(b[12]), .gt(fullcomparator_1_gt_out), .lt(fullcomparator_1_lt_out),
    .eq(fullcomparator_1_eq_out), .gt_out(fullcomparator_5_gt_out), .lt_out(fullcomparator_5_lt_out),
    .eq_out(fullcomparator_5_eq_out));
  fullComparator fullcomparator_6 (
    .a(a[8]), .b(b[8]), .gt(fullcomparator_2_gt_out), .lt(fullcomparator_2_lt_out),
    .eq(fullcomparator_2_eq_out), .gt_out(fullcomparator_6_gt_out), .lt_out(fullcomparator_6_lt_out),
    .eq_out(fullcomparator_6_eq_out));
  fullComparator fullcomparator_7 (
    .a(a[4]), .b(b[4]), .gt(fullcomparator_3_gt_out), .lt(fullcomparator_3_lt_out),
    .eq(fullcomparator_3_eq_out), .gt_out(fullcomparator_7_gt_out), .lt_out(fullcomparator_7_lt_out),
    .eq_out(fullcomparator_7_eq_out));
  fullComparator fullcomparator_8 (
    .a(a[15]), .b(b[15]), .gt(fullcomparator_4_gt_out), .lt(fullcomparator_4_lt_out),
    .eq(fullcomparator_4_eq_out), .gt_out(fullcomparator_8_gt_out), .lt_out(fullcomparator_8_lt_out),
    .eq_out(fullcomparator_8_eq_out));
  fullComparator fullcomparator_9 (
    .a(a[11]), .b(b[11]), .gt(fullcomparator_5_gt_out), .lt(fullcomparator_5_lt_out),
    .eq(fullcomparator_5_eq_out), .gt_out(fullcomparator_9_gt_out), .lt_out(fullcomparator_9_lt_out),
    .eq_out(fullcomparator_9_eq_out));
  fullComparator fullcomparator_10 (
    .a(a[7]), .b(b[7]), .gt(fullcomparator_6_gt_out), .lt(fullcomparator_6_lt_out),
    .eq(fullcomparator_6_eq_out), .gt_out(fullcomparator_10_gt_out), .lt_out(fullcomparator_10_lt_out),
    .eq_out(fullcomparator_10_eq_out));
  fullComparator fullcomparator_11 (
    .a(a[3]), .b(b[3]), .gt(fullcomparator_7_gt_out), .lt(fullcomparator_7_lt_out),
    .eq(fullcomparator_7_eq_out), .gt_out(fullcomparator_11_gt_out), .lt_out(fullcomparator_11_lt_out),
    .eq_out(fullcomparator_11_eq_out));
  fullComparator fullcomparator_12 (
    .a(a[14]), .b(b[14]), .gt(fullcomparator_8_gt_out), .lt(fullcomparator_8_lt_out),
    .eq(fullcomparator_8_eq_out), .gt_out(fullcomparator_12_gt_out), .lt_out(fullcomparator_12_lt_out),
    .eq_out(fullcomparator_12_eq_out));
  fullComparator fullcomparator_13 (
    .a(a[10]), .b(b[10]), .gt(fullcomparator_9_gt_out), .lt(fullcomparator_9_lt_out),
    .eq(fullcomparator_9_eq_out), .gt_out(fullcomparator_13_gt_out), .lt_out(fullcomparator_13_lt_out),
    .eq_out(fullcomparator_13_eq_out));
  fullComparator fullcomparator_14 (
    .a(a[6]), .b(b[6]), .gt(fullcomparator_10_gt_out), .lt(fullcomparator_10_lt_out),
    .eq(fullcomparator_10_eq_out), .gt_out(fullcomparator_14_gt_out), .lt_out(fullcomparator_14_lt_out),
    .eq_out(fullcomparator_14_eq_out));
  fullComparator fullcomparator_15 (
    .a(a[2]), .b(b[2]), .gt(fullcomparator_11_gt_out), .lt(fullcomparator_11_lt_out),
    .eq(fullcomparator_11_eq_out), .gt_out(fullcomparator_15_gt_out), .lt_out(fullcomparator_15_lt_out),
    .eq_out(fullcomparator_15_eq_out));
  fullComparator fullcomparator_16 (
    .a(a[1]), .b(b[1]), .gt(fullcomparator_15_gt_out), .lt(fullcomparator_15_lt_out),
    .eq(fullcomparator_15_eq_out), .gt_out(fullcomparator_16_gt_out), .lt_out(fullcomparator_16_lt_out),
    .eq_out(fullcomparator_16_eq_out));
  fullComparator fullcomparator_17 (
    .a(a[0]), .b(b[0]), .gt(fullcomparator_16_gt_out), .lt(fullcomparator_16_lt_out),
    .eq(fullcomparator_16_eq_out), .gt_out(gt), .lt_out(lt), .eq_out(eq));

  // Other names for the same wires on the sheet: a_0 = a[0]; a_1 = a[1]; a_2 = a[2]; a_3 = a[3]; a_4 = a[4];
  //   a_5 = a[5]; a_6 = a[6]; a_7 = a[7]; a_8 = a[8]; a_9 = a[9]; a_10 = a[10]; a_11 = a[11]; a_12 = a[12];
  //   a_13 = a[13]; a_14 = a[14]; a_15 = a[15]; a_16 = a[16]; a_17 = a[17]; b_0 = b[0]; b_1 = b[1]; b_2 = b[2];
  //   b_3 = b[3]; b_4 = b[4]; b_5 = b[5]; b_6 = b[6]; b_7 = b[7]; b_8 = b[8]; b_9 = b[9]; b_10 = b[10]; b_11 = b[11];
  //   b_12 = b[12]; b_13 = b[13]; b_14 = b[14]; b_15 = b[15]; b_16 = b[16]; b_17 = b[17]
endmodule

module _4bitComparator (
  input  [3:0] a,
  input  [3:0] b,
  output gt,
  output lt,
  output eq
);

  wire fullcomparator_1_eq_out, fullcomparator_1_gt_out, fullcomparator_1_lt_out, fullcomparator_2_eq_out,
       fullcomparator_2_gt_out, fullcomparator_2_lt_out, halfcomparator_1_eq_out, halfcomparator_1_gt_out,
       halfcomparator_1_lt_out;

  halfComparator halfcomparator_1 (
    .A(a[3]), .B(b[3]), .gt_out(halfcomparator_1_gt_out), .lt_out(halfcomparator_1_lt_out),
    .eq_out(halfcomparator_1_eq_out));
  fullComparator fullcomparator_1 (
    .a(a[2]), .b(b[2]), .gt(halfcomparator_1_gt_out), .lt(halfcomparator_1_lt_out),
    .eq(halfcomparator_1_eq_out), .gt_out(fullcomparator_1_gt_out), .lt_out(fullcomparator_1_lt_out),
    .eq_out(fullcomparator_1_eq_out));
  fullComparator fullcomparator_2 (
    .a(a[1]), .b(b[1]), .gt(fullcomparator_1_gt_out), .lt(fullcomparator_1_lt_out),
    .eq(fullcomparator_1_eq_out), .gt_out(fullcomparator_2_gt_out), .lt_out(fullcomparator_2_lt_out),
    .eq_out(fullcomparator_2_eq_out));
  fullComparator fullcomparator_3 (
    .a(a[0]), .b(b[0]), .gt(fullcomparator_2_gt_out), .lt(fullcomparator_2_lt_out),
    .eq(fullcomparator_2_eq_out), .gt_out(gt), .lt_out(lt), .eq_out(eq));

  // Other names for the same wires on the sheet: a_0 = a[0]; a_1 = a[1]; a_2 = a[2]; a_3 = a[3]; b_0 = b[0];
  //   b_1 = b[1]; b_2 = b[2]; b_3 = b[3]
endmodule

module ALU (
  input  [17:0] A,
  input  [17:0] B,
  input  [1:0] ALU_operation,
  output carry_out,
  output [17:0] \output 
);

  wire [17:0] AND_out, n18bitadder_1_sum, NAND_out, NOR_out;

  _18bitAdder u_18bitadder_1 (.A(A), .B(B), .carry_in(1'b0), .carry_out(carry_out), .sum(n18bitadder_1_sum));
  assign AND_out = A & B;  // AND_Gate AND, 18 bits wide
  assign NAND_out = ~(A & B);  // NAND_Gate NAND, 18 bits wide
  assign NOR_out = ~(A | B);  // NOR_Gate NOR, 18 bits wide
  Multiplexer #(.select(2), .width(18), .enable("false")) multiplexer_1 (
    .in0(n18bitadder_1_sum), .in1(AND_out), .in2(NAND_out), .in3(NOR_out), .out(\output ), .sel(ALU_operation));
endmodule

module _2bitAdder (
  input  [1:0] A,
  input  [1:0] B,
  input  carry_in,
  output carry_out,
  output [1:0] sum
);

  wire fulladder_1_carry_out;

  fullAdder fulladder_1 (.A(A[0]), .B(B[0]), .carry_in(carry_in), .sum(sum[0]), .carry_out(fulladder_1_carry_out));
  fullAdder fulladder_2 (.A(A[1]), .B(B[1]), .carry_in(fulladder_1_carry_out), .sum(sum[1]), .carry_out(carry_out));
endmodule

module _4bitAdder (
  input  [3:0] A,
  input  [3:0] B,
  input  carry_in,
  output carry_out,
  output [3:0] sum
);

  wire fulladder_1_carry_out, fulladder_2_carry_out, fulladder_3_carry_out;

  fullAdder fulladder_1 (.A(A[0]), .B(B[0]), .carry_in(carry_in), .sum(sum[0]), .carry_out(fulladder_1_carry_out));
  fullAdder fulladder_2 (
    .A(A[1]), .B(B[1]), .carry_in(fulladder_1_carry_out), .sum(sum[1]), .carry_out(fulladder_2_carry_out));
  fullAdder fulladder_3 (
    .A(A[2]), .B(B[2]), .carry_in(fulladder_2_carry_out), .sum(sum[2]), .carry_out(fulladder_3_carry_out));
  fullAdder fulladder_4 (.A(A[3]), .B(B[3]), .carry_in(fulladder_3_carry_out), .sum(sum[3]), .carry_out(carry_out));
endmodule

module fullAdder (
  input  A,
  input  B,
  input  carry_in,
  output sum,
  output carry_out
);

  wire and_1_out, and_2_out, xor_1_out;

  xor xor_1 (xor_1_out, A, B);
  xor xor_2 (sum, xor_1_out, carry_in);
  and and_1 (and_1_out, carry_in, xor_1_out);
  and and_2 (and_2_out, B, A);
  or or_1 (carry_out, and_1_out, and_2_out);
endmodule

module _8bitAdder (
  input  [7:0] A,
  input  [7:0] B,
  input  carry_in,
  output carry_out,
  output [7:0] sum
);

  wire n4bitadder_2_carry_out;

  _4bitAdder u_4bitadder_1 (
    .A(A[7:4]), .B(B[7:4]), .carry_in(n4bitadder_2_carry_out), .carry_out(carry_out), .sum(sum[7:4]));
  _4bitAdder u_4bitadder_2 (
    .A(A[3:0]), .B(B[3:0]), .carry_in(carry_in), .carry_out(n4bitadder_2_carry_out), .sum(sum[3:0]));
endmodule

module _18bitAdder (
  input  [17:0] A,
  input  [17:0] B,
  input  carry_in,
  output carry_out,
  output [17:0] sum
);

  wire n2bitadder_1_carry_out, n2bitadder_2_carry_out, n2bitadder_3_carry_out, n2bitadder_4_carry_out,
       n2bitadder_5_carry_out, n2bitadder_6_carry_out, n2bitadder_7_carry_out, n2bitadder_8_carry_out;

  _2bitAdder u_2bitadder_1 (
    .A(A[1:0]), .B(B[1:0]), .carry_in(carry_in), .carry_out(n2bitadder_1_carry_out), .sum(sum[1:0]));
  _2bitAdder u_2bitadder_2 (
    .A(A[3:2]), .B(B[3:2]), .carry_in(n2bitadder_1_carry_out), .carry_out(n2bitadder_2_carry_out),
    .sum(sum[3:2]));
  _2bitAdder u_2bitadder_3 (
    .A(A[5:4]), .B(B[5:4]), .carry_in(n2bitadder_2_carry_out), .carry_out(n2bitadder_3_carry_out),
    .sum(sum[5:4]));
  _2bitAdder u_2bitadder_4 (
    .A(A[7:6]), .B(B[7:6]), .carry_in(n2bitadder_3_carry_out), .carry_out(n2bitadder_4_carry_out),
    .sum(sum[7:6]));
  _2bitAdder u_2bitadder_5 (
    .A(A[9:8]), .B(B[9:8]), .carry_in(n2bitadder_4_carry_out), .carry_out(n2bitadder_5_carry_out),
    .sum(sum[9:8]));
  _2bitAdder u_2bitadder_6 (
    .A(A[11:10]), .B(B[11:10]), .carry_in(n2bitadder_5_carry_out), .carry_out(n2bitadder_6_carry_out),
    .sum(sum[11:10]));
  _2bitAdder u_2bitadder_7 (
    .A(A[13:12]), .B(B[13:12]), .carry_in(n2bitadder_6_carry_out), .carry_out(n2bitadder_7_carry_out),
    .sum(sum[13:12]));
  _2bitAdder u_2bitadder_8 (
    .A(A[15:14]), .B(B[15:14]), .carry_in(n2bitadder_7_carry_out), .carry_out(n2bitadder_8_carry_out),
    .sum(sum[15:14]));
  _2bitAdder u_2bitadder_9 (
    .A(A[17:16]), .B(B[17:16]), .carry_in(n2bitadder_8_carry_out), .carry_out(carry_out), .sum(sum[17:16]));
endmodule

module extend6to18 (
  input  [5:0] in_1,
  output [17:0] out_2
);

  Multiplexer #(.width(12), .enable("false")) multiplexer_1 (
    .in0({12{1'b0}}), .in1({12{1'b1}}), .out(out_2[17:6]), .sel(in_1[5]));

  assign out_2[5:0] = in_1;

  // Other names for the same wires on the sheet: value[4:0] = in_1[4:0]; sign = in_1[5]; extend[11:0] = out_2[17:6]
endmodule

module extend10to18 (
  input  [9:0] in_1,
  output [17:0] out_2
);

  Multiplexer #(.width(8), .enable("false")) multiplexer_1 (
    .in0({8{1'b0}}), .in1({8{1'b1}}), .out(out_2[17:10]), .sel(in_1[9]));

  assign out_2[9:0] = in_1;

  // Other names for the same wires on the sheet: value[8:0] = in_1[8:0]; sign = in_1[9]; extend[7:0] = out_2[17:10]
endmodule

module dLatch (
  input  D,
  input  c,
  output Q
);

  wire and_1_out, and_2_out, halfadder_1_c_out, halfadder_1_sum, multiplexer_1_out, nand_1_out, nor_1_out,
       not_1_out, register_1_q;

  not not_1 (not_1_out, D);
  halfAdder halfadder_1 (.in_1(c), .in_2(register_1_q), .sum(halfadder_1_sum), .c_out(halfadder_1_c_out));
  nand nand_1 (nand_1_out, halfadder_1_sum, halfadder_1_c_out);
  and and_1 (and_1_out, D, c);
  and and_2 (and_2_out, c, not_1_out);
  Register #(.width(1)) register_1 (.D(nand_1_out), .en(1'b1), .Q(register_1_q), .clk(c));  // open: clr
  nor nor_1 (nor_1_out, and_1_out, Q);
  nor nor_2 (Q, multiplexer_1_out, and_2_out);
  Multiplexer #(.enable("false")) multiplexer_1 (
    .in0(1'b1), .in1(nor_1_out), .out(multiplexer_1_out), .sel(register_1_q));
endmodule

module dFlipFlop (
  input  D,
  input  clk,
  output out_3
);

  wire dlatch_1_q, not_1_out;

  not not_1 (not_1_out, clk);
  dLatch dlatch_1 (.D(D), .c(not_1_out), .Q(dlatch_1_q));
  dLatch dlatch_2 (.D(dlatch_1_q), .c(clk), .Q(out_3));
endmodule

module _2_sNegativeToPositive (
  input  [17:0] in_1,
  output [17:0] out_2
);

  wire [17:0] negator_1_out;

  Negator #(.width(18)) negator_1 (.in(in_1), .out(negator_1_out));
  Multiplexer #(.width(18)) multiplexer_1 (.in0(in_1), .in1(negator_1_out), .out(out_2), .sel(in_1[17]));  // open: en
endmodule

// COUNTER
module ProgramCounter (
  input  in_1,
  input  in_2,
  input  in_3,
  input  [17:0] \input ,
  input  reset,
  output [17:0] \output 
);

  wire load_enable, not_1_out, or_1_out;
  wire [17:0] added_value, n2_snegativetopositive_1_out_2, substracted_value, value_load;

  not not_1 (not_1_out, in_1);
  or or_1 (or_1_out, in_2, \input [17]);
  and and_1 (load_enable, not_1_out, or_1_out);
  Counter #(.width(18), .max('h3ffff)) counter_1 (
    .load(load_enable), .D(value_load), .count(in_1), .Q(\output ), .clk(in_3), .clr(reset));  // open: carry
  _2_sNegativeToPositive u_2_snegativetopositive_1 (.in_1(\input ), .out_2(n2_snegativetopositive_1_out_2));
  _18bitAdder u_18bitadder_1 (.A(\input ), .B(\output ), .carry_in(1'b0), .sum(added_value));  // open: carry_out
  Subtractor #(.width(18)) subtractor_1 (
    .a(\output ), .b(n2_snegativetopositive_1_out_2), .out(substracted_value));  // open: bin, bout
  assign value_load = in_2 ? added_value : 18'bz;  // Controlled_Buffer controlled_buffer_1
  assign value_load = \input [17] ? substracted_value : 18'bz;  // Controlled_Buffer controlled_buffer_2

  // Other names for the same wires on the sheet: clock = in_3; substract = \input [17]; jump = in_2; count = in_1;
  //   next = in_1

  // Notes on the sheet:
  //   increment by 1
endmodule

// COMPARE
module Compare (
  input  [17:0] in_1,
  input  [17:0] in_2,
  output ZF,
  output CF
);

  wire GE, GT, LE, n18bitcomparator_1_eq, n18bitcomparator_1_gt, n18bitcomparator_1_lt, not_1_out, not_2_out,
       not_3_out, not_4_out;

  _18bitComparator u_18bitcomparator_1 (
    .b(in_2), .a(in_1), .gt(n18bitcomparator_1_gt), .lt(n18bitcomparator_1_lt), .eq(n18bitcomparator_1_eq));
  not not_1 (not_1_out, n18bitcomparator_1_eq);
  not not_2 (not_2_out, n18bitcomparator_1_gt);
  not not_3 (not_3_out, n18bitcomparator_1_lt);
  not not_4 (not_4_out, n18bitcomparator_1_eq);
  or or_1 (GE, n18bitcomparator_1_gt, n18bitcomparator_1_eq);
  and and_1 (GT, n18bitcomparator_1_gt, not_1_out);
  and and_2 (ZF, not_2_out, n18bitcomparator_1_eq, not_3_out);
  and and_3 (CF, not_4_out, n18bitcomparator_1_lt);
  or or_2 (LE, n18bitcomparator_1_eq, n18bitcomparator_1_lt);

  // Other names for the same wires on the sheet: E = ZF; LT = CF

  // Notes on the sheet:
  //   OP1 > OP2  ZF0 CF0
  //   OP1 = OP2  ZF1 CF0
  //   OP1 < OP2  ZF0 CF1
  //   OP1 >= OP2    CF0
  //   OP1 <= OP2  ZF1 or CF1
endmodule

module _18BitsRegister (
  input  [17:0] in_1,
  input  enable,
  input  clear,
  input  clock,
  output [17:0] out_5
);

  wire multiplexer_1_out, multiplexer_2_out, multiplexer_3_out, multiplexer_4_out, multiplexer_5_out,
       multiplexer_6_out, multiplexer_7_out, multiplexer_8_out, multiplexer_9_out, multiplexer_10_out,
       multiplexer_11_out, multiplexer_12_out, multiplexer_13_out, multiplexer_14_out, multiplexer_15_out,
       multiplexer_16_out, multiplexer_17_out, multiplexer_18_out;
  wire [0:0] not_1_out;

  not not_1 (not_1_out[0], enable);
  Multiplexer #(.select(2), .enable("false")) multiplexer_1 (
    .in0(in_1[0]), .in1(out_5[0]), .in2(1'b0), .in3(1'b0), .out(multiplexer_1_out),
    .sel({clear, not_1_out[0]}));
  dFlipFlop dflipflop_1 (.D(multiplexer_1_out), .clk(clock), .out_3(out_5[0]));
  Multiplexer #(.select(2), .enable("false")) multiplexer_2 (
    .in0(in_1[9]), .in1(out_5[9]), .in2(1'b0), .in3(1'b0), .out(multiplexer_2_out),
    .sel({clear, not_1_out[0]}));
  dFlipFlop dflipflop_2 (.D(multiplexer_2_out), .clk(clock), .out_3(out_5[9]));
  Multiplexer #(.select(2), .enable("false")) multiplexer_3 (
    .in0(in_1[1]), .in1(out_5[1]), .in2(1'b0), .in3(1'b0), .out(multiplexer_3_out),
    .sel({clear, not_1_out[0]}));
  dFlipFlop dflipflop_3 (.D(multiplexer_3_out), .clk(clock), .out_3(out_5[1]));
  Multiplexer #(.select(2), .enable("false")) multiplexer_4 (
    .in0(in_1[10]), .in1(out_5[10]), .in2(1'b0), .in3(1'b0), .out(multiplexer_4_out),
    .sel({clear, not_1_out[0]}));
  dFlipFlop dflipflop_4 (.D(multiplexer_4_out), .clk(clock), .out_3(out_5[10]));
  Multiplexer #(.select(2), .enable("false")) multiplexer_5 (
    .in0(in_1[2]), .in1(out_5[2]), .in2(1'b0), .in3(1'b0), .out(multiplexer_5_out),
    .sel({clear, not_1_out[0]}));
  dFlipFlop dflipflop_5 (.D(multiplexer_5_out), .clk(clock), .out_3(out_5[2]));
  Multiplexer #(.select(2), .enable("false")) multiplexer_6 (
    .in0(in_1[11]), .in1(out_5[11]), .in2(1'b0), .in3(1'b0), .out(multiplexer_6_out),
    .sel({clear, not_1_out[0]}));
  dFlipFlop dflipflop_6 (.D(multiplexer_6_out), .clk(clock), .out_3(out_5[11]));
  Multiplexer #(.select(2), .enable("false")) multiplexer_7 (
    .in0(in_1[3]), .in1(out_5[3]), .in2(1'b0), .in3(1'b0), .out(multiplexer_7_out),
    .sel({clear, not_1_out[0]}));
  dFlipFlop dflipflop_7 (.D(multiplexer_7_out), .clk(clock), .out_3(out_5[3]));
  Multiplexer #(.select(2), .enable("false")) multiplexer_8 (
    .in0(in_1[12]), .in1(out_5[12]), .in2(1'b0), .in3(1'b0), .out(multiplexer_8_out),
    .sel({clear, not_1_out[0]}));
  dFlipFlop dflipflop_8 (.D(multiplexer_8_out), .clk(clock), .out_3(out_5[12]));
  Multiplexer #(.select(2), .enable("false")) multiplexer_9 (
    .in0(in_1[4]), .in1(out_5[4]), .in2(1'b0), .in3(1'b0), .out(multiplexer_9_out),
    .sel({clear, not_1_out[0]}));
  Multiplexer #(.select(2), .enable("false")) multiplexer_10 (
    .in0(in_1[13]), .in1(out_5[13]), .in2(1'b0), .in3(1'b0), .out(multiplexer_10_out),
    .sel({clear, not_1_out[0]}));
  dFlipFlop dflipflop_9 (.D(multiplexer_9_out), .clk(clock), .out_3(out_5[4]));
  dFlipFlop dflipflop_10 (.D(multiplexer_10_out), .clk(clock), .out_3(out_5[13]));
  Multiplexer #(.select(2), .enable("false")) multiplexer_11 (
    .in0(in_1[5]), .in1(out_5[5]), .in2(1'b0), .in3(1'b0), .out(multiplexer_11_out),
    .sel({clear, not_1_out[0]}));
  dFlipFlop dflipflop_11 (.D(multiplexer_11_out), .clk(clock), .out_3(out_5[5]));
  Multiplexer #(.select(2), .enable("false")) multiplexer_12 (
    .in0(in_1[14]), .in1(out_5[14]), .in2(1'b0), .in3(1'b0), .out(multiplexer_12_out),
    .sel({clear, not_1_out[0]}));
  dFlipFlop dflipflop_12 (.D(multiplexer_12_out), .clk(clock), .out_3(out_5[14]));
  Multiplexer #(.select(2), .enable("false")) multiplexer_13 (
    .in0(in_1[6]), .in1(out_5[6]), .in2(1'b0), .in3(1'b0), .out(multiplexer_13_out),
    .sel({clear, not_1_out[0]}));
  dFlipFlop dflipflop_13 (.D(multiplexer_13_out), .clk(clock), .out_3(out_5[6]));
  Multiplexer #(.select(2), .enable("false")) multiplexer_14 (
    .in0(in_1[15]), .in1(out_5[15]), .in2(1'b0), .in3(1'b0), .out(multiplexer_14_out),
    .sel({clear, not_1_out[0]}));
  dFlipFlop dflipflop_14 (.D(multiplexer_14_out), .clk(clock), .out_3(out_5[15]));
  Multiplexer #(.select(2), .enable("false")) multiplexer_15 (
    .in0(in_1[16]), .in1(out_5[16]), .in2(1'b0), .in3(1'b0), .out(multiplexer_15_out),
    .sel({clear, not_1_out[0]}));
  Multiplexer #(.select(2), .enable("false")) multiplexer_16 (
    .in0(in_1[7]), .in1(out_5[7]), .in2(1'b0), .in3(1'b0), .out(multiplexer_16_out),
    .sel({clear, not_1_out[0]}));
  dFlipFlop dflipflop_15 (.D(multiplexer_16_out), .clk(clock), .out_3(out_5[7]));
  dFlipFlop dflipflop_16 (.D(multiplexer_15_out), .clk(clock), .out_3(out_5[16]));
  Multiplexer #(.select(2), .enable("false")) multiplexer_17 (
    .in0(in_1[8]), .in1(out_5[8]), .in2(1'b0), .in3(1'b0), .out(multiplexer_17_out),
    .sel({clear, not_1_out[0]}));
  dFlipFlop dflipflop_17 (.D(multiplexer_17_out), .clk(clock), .out_3(out_5[8]));
  Multiplexer #(.select(2), .enable("false")) multiplexer_18 (
    .in0(in_1[17]), .in1(out_5[17]), .in2(1'b0), .in3(1'b0), .out(multiplexer_18_out),
    .sel({clear, not_1_out[0]}));
  dFlipFlop dflipflop_18 (.D(multiplexer_18_out), .clk(clock), .out_3(out_5[17]));
endmodule

module halfAdder (
  input  in_1,
  input  in_2,
  output sum,
  output c_out
);

  xor xor_1 (sum, in_1, in_2);
  and and_1 (c_out, in_1, in_2);
endmodule

// CONTROL UNIT
module controlUnit (
  input  [17:0] input_18,
  input  [17:0] register1_input,
  input  [17:0] register2_input,
  output [3:0] src2_op2,
  output write_memory,
  output [3:0] src1,
  output [3:0] op1,
  output [3:0] dest_st_src1,
  output read_memory,
  output [5:0] imm6,
  output [9:0] address10,
  output isImmediate,
  output [1:0] alu_op,
  output [17:0] address18,
  output [17:0] imm18,
  output isALU,
  output write_register,
  output [2:0] jump_type,
  output is_cmp_successful,
  output is_cmp,
  output is_jump
);

  wire ADD, ADDI, AND, and_1_out, and_2_out, and_3_out, and_4_out, and_5_out, ANDI, CMP, JA, JAE, JB, JBE,
       JE, n18bitcomparator_1_eq, n18bitcomparator_1_gt, n18bitcomparator_1_lt, NAND, NOR, or_1_out,
       or_2_out, or_7_out, or_8_out;

  extend10to18 extend10to18_1 (.in_1(input_18[9:0]), .out_2(address18));
  _18bitComparator u_18bitcomparator_1 (
    .b(register2_input), .a(register1_input), .gt(n18bitcomparator_1_gt), .lt(n18bitcomparator_1_lt),
    .eq(n18bitcomparator_1_eq));
  or or_1 (or_1_out, n18bitcomparator_1_eq, n18bitcomparator_1_gt);
  extend6to18 extend6to18_1 (.in_1(input_18[5:0]), .out_2(imm18));
  or or_2 (or_2_out, n18bitcomparator_1_eq, n18bitcomparator_1_lt);
  and and_1 (and_1_out, JAE, or_1_out);
  and and_2 (and_2_out, JBE, or_2_out);
  and and_3 (and_3_out, JA, n18bitcomparator_1_gt);
  and and_4 (and_4_out, JB, n18bitcomparator_1_lt);
  and and_5 (and_5_out, n18bitcomparator_1_eq, JE);
  or or_3 (is_cmp_successful, and_1_out, and_2_out, and_3_out, and_4_out, and_5_out);
  or or_4 (isImmediate, ADDI, ANDI);
  or or_5 (write_register, isALU, read_memory);
  Decoder #(.select(4)) decoder_1 (
    .out0(ADD), .out1(AND), .out2(NAND), .out3(NOR), .out4(ADDI), .out5(ANDI), .out6(read_memory),
    .out7(write_memory), .out8(CMP), .out9(is_jump), .out10(JE), .out11(JA), .out12(JB), .out13(JAE),
    .out14(JBE), .sel(input_18[17:14]), .en(1'b1));  // open: out15
  or or_6 (is_cmp, CMP, JAE, JBE, JA, JB, JE);
  or or_7 (or_7_out, ADD, ADDI);
  or or_8 (or_8_out, AND, ANDI);
  Priority_Encoder #(.select(2)) priority_encoder_1 (
    .in0(or_7_out), .in1(or_8_out), .in2(NAND), .in3(NOR), .out(alu_op));  // open: gs, en_out, en_in
  or or_9 (isALU, or_7_out, or_8_out, NAND, NOR);
  Priority_Encoder priority_encoder_2 (
    .in0(is_jump), .in1(JE), .in2(JA), .in3(JB), .in4(JAE), .in5(JBE), .out(jump_type));  // open: in6, in7, en_in, gs, en_out

  assign address10 = input_18[9:0];
  assign dest_st_src1 = input_18[13:10];
  assign imm6 = input_18[5:0];
  assign op1 = input_18[7:4];
  assign src1 = input_18[9:6];
  assign src2_op2 = input_18[3:0];

  // Other names for the same wires on the sheet: address_10[9:0] = input_18[9:0]; address_18[17:0] = address18;
  //   alu = isALU; imm[5:0] = input_18[5:0]; op2[3:0] = input_18[3:0]; src2[3:0] = input_18[3:0];
  //   imm_18[17:0] = imm18; JUMP = is_jump; LD = read_memory; opcode[3:0] = input_18[17:14]; ST = write_memory;
  //   dest[3:0] = input_18[13:10]; st_src1[3:0] = input_18[13:10]
endmodule
